# Fritzing sketch DiagramaElectroMecanico (saved by Fritzing 0.9.3b)
breadboards: 1

parts:
  VCC1 = Battery
  Componente3 = Bluetooth HC-06
  M3 = Getriebemotor
  M4 = Getriebemotor
  M5 = DC Motor
  KY-2 = Keyes Relay [package=THT]
  VCC2 = Battery
  Componente1 = Arduino Uno (Rev3)
  S1 = H-Bridge with L298N

nets:
  N1: VCC1.+, S1.12V
  N2: Componente3.RXD, Componente1.D1/TX
  N3: Componente3.TXD, Componente1.D0/RX
  GND: Componente3.GND, KY-2.ground, Componente1.GND, S1.GND
  VCC: Componente3.VCC, KY-2.power, Componente1.3V3
  N4: M3.pin_1, S1.OUT1-Motor1
  N5: M3.pin_2, S1.OUT2-Motor1
  N6: M4.pin_1, S1.OUT4-Motor2
  N7: M4.pin_2, S1.OUT3-Motor2
  N8: M5.pin_1, KY-2.NO
  N9: M5.pin_2, VCC2.-
  N10: KY-2.signal, Componente1.D4
  N11: KY-2.C, VCC2.+
  N12: Componente1.D9_PWM, S1.IN2
  N13: Componente1.D10_PWM/SS, S1.IN1
  N14: Componente1.D5_PWM, S1.IN4
  N15: Componente1.D6_PWM, S1.IN3
  5V: Componente1.5V, S1.5V

custom parts:
  Battery: Your standard 2x 18650 battery pack (7,4 Volts)
  Keyes Relay: The Keyes 5V relay module is suitable for SCM development, home appliance control. It uses a 5V~12V TIL control signal which can control DC / AC signal.
  H-Bridge with L298N: h-bridge
